// Logisim project scpu.circ as structural Verilog: 2 circuits, main circuit Read_Only_memory
module Read_Only_memory (
  input  RESET,
  input  A2,
  input  A1,
  input  A0,
  input  ENABLE,
  output Q4,
  output Q0,
  output Q6,
  output Q5,
  output Q2,
  output Q1,
  output Q7,
  output Q3
);

  wire and_1_out, and_2_out, and_3_out, and_4_out, and_5_out, and_6_out, and_7_out, and_8_out, and_9_out,
       and_10_out, and_11_out, and_12_out, and_13_out, and_14_out, and_15_out, and_16_out, and_17_out,
       and_18_out, and_19_out, and_20_out, and_21_out, and_22_out, and_23_out, and_24_out, and_25_out,
       and_26_out, and_27_out, and_28_out, and_29_out, and_30_out, and_31_out, and_32_out, and_33_out,
       and_34_out, and_35_out, and_36_out, and_37_out, and_38_out, and_39_out, and_40_out, and_41_out,
       and_42_out, and_43_out, and_44_out, and_45_out, and_46_out, and_47_out, and_48_out, and_49_out,
       and_50_out, and_51_out, and_52_out, and_53_out, and_54_out, and_55_out, and_56_out, and_57_out,
       and_58_out, and_59_out, and_60_out, and_61_out, and_62_out, and_63_out, and_64_out, CLK_out,
       decoder_1_out0, decoder_1_out1, decoder_1_out2, decoder_1_out3, decoder_1_out4, decoder_1_out5,
       decoder_1_out6, decoder_1_out7;
  wire [2:0] register_8bit_1_q0;

  Clock CLK (.out(CLK_out));
  Register_8bit register_8bit_1 (
    .CLK(CLK_out), .RESET(RESET), .D2(A2), .D1(A1), .D0(A0), .ENABLE(ENABLE), .Q2(register_8bit_1_q0[2]),
    .Q1(register_8bit_1_q0[1]), .Q0(register_8bit_1_q0[0]));  // open: D7, D6, D5, D4, D3, Q7, Q6, Q5, Q4, Q3
  Decoder #(.select(3)) decoder_1 (
    .out0(decoder_1_out0), .out1(decoder_1_out1), .out2(decoder_1_out2), .out3(decoder_1_out3),
    .out4(decoder_1_out4), .out5(decoder_1_out5), .out6(decoder_1_out6), .out7(decoder_1_out7),
    .sel(register_8bit_1_q0), .en(1'b1));
  or or_1 (Q7, and_1_out, and_2_out, and_3_out, and_4_out, and_5_out, and_6_out, and_7_out, and_8_out);
  and and_1 (and_1_out, decoder_1_out0, 1'b1);
  and and_2 (and_2_out, decoder_1_out1, 1'b1);
  and and_3 (and_3_out, decoder_1_out2, 1'b1);
  and and_4 (and_4_out, decoder_1_out3, 1'b1);
  and and_5 (and_5_out, decoder_1_out4, 1'b0);
  and and_6 (and_6_out, decoder_1_out5, 1'b0);
  and and_7 (and_7_out, decoder_1_out6, 1'b1);
  and and_8 (and_8_out, decoder_1_out7, 1'b1);
  and and_9 (and_9_out, decoder_1_out0, 1'b0);
  and and_10 (and_10_out, decoder_1_out1, 1'b0);
  and and_11 (and_11_out, decoder_1_out2, 1'b0);
  and and_12 (and_12_out, decoder_1_out3, 1'b0);
  and and_13 (and_13_out, decoder_1_out4, 1'b0);
  and and_14 (and_14_out, decoder_1_out5, 1'b0);
  and and_15 (and_15_out, decoder_1_out6, 1'b1);
  and and_16 (and_16_out, decoder_1_out7, 1'b1);
  or or_2 (Q6, and_9_out, and_10_out, and_11_out, and_12_out, and_13_out, and_14_out, and_15_out, and_16_out);
  and and_17 (and_17_out, decoder_1_out0, 1'b0);
  and and_18 (and_18_out, decoder_1_out1, 1'b0);
  and and_19 (and_19_out, decoder_1_out2, 1'b1);
  and and_20 (and_20_out, decoder_1_out3, 1'b1);
  and and_21 (and_21_out, decoder_1_out4, 1'b0);
  and and_22 (and_22_out, decoder_1_out5, 1'b1);
  and and_23 (and_23_out, decoder_1_out6, 1'b0);
  and and_24 (and_24_out, decoder_1_out7, 1'b0);
  or or_3 (Q5, and_17_out, and_18_out, and_19_out, and_20_out, and_21_out, and_22_out, and_23_out, and_24_out);
  and and_25 (and_25_out, decoder_1_out0, 1'b0);
  and and_26 (and_26_out, decoder_1_out1, 1'b1);
  and and_27 (and_27_out, decoder_1_out2, 1'b0);
  and and_28 (and_28_out, decoder_1_out3, 1'b1);
  and and_29 (and_29_out, decoder_1_out4, 1'b1);
  and and_30 (and_30_out, decoder_1_out5, 1'b0);
  and and_31 (and_31_out, decoder_1_out6, 1'b1);
  and and_32 (and_32_out, decoder_1_out7, 1'b1);
  and and_33 (and_33_out, decoder_1_out0, 1'b1);
  and and_34 (and_34_out, decoder_1_out1, 1'b0);
  and and_35 (and_35_out, decoder_1_out2, 1'b0);
  and and_36 (and_36_out, decoder_1_out3, 1'b0);
  and and_37 (and_37_out, decoder_1_out4, 1'b0);
  and and_38 (and_38_out, decoder_1_out5, 1'b1);
  and and_39 (and_39_out, decoder_1_out6, 1'b0);
  and and_40 (and_40_out, decoder_1_out7, 1'b1);
  or or_4 (Q4, and_25_out, and_26_out, and_27_out, and_28_out, and_29_out, and_30_out, and_31_out, and_32_out);
  and and_41 (and_41_out, decoder_1_out0, 1'b0);
  and and_42 (and_42_out, decoder_1_out1, 1'b0);
  and and_43 (and_43_out, decoder_1_out2, 1'b0);
  and and_44 (and_44_out, decoder_1_out3, 1'b0);
  and and_45 (and_45_out, decoder_1_out4, 1'b1);
  and and_46 (and_46_out, decoder_1_out5, 1'b0);
  and and_47 (and_47_out, decoder_1_out6, 1'b0);
  and and_48 (and_48_out, decoder_1_out7, 1'b1);
  or or_5 (Q3, and_33_out, and_34_out, and_35_out, and_36_out, and_37_out, and_38_out, and_39_out, and_40_out);
  and and_49 (and_49_out, decoder_1_out0, 1'b1);
  and and_50 (and_50_out, decoder_1_out1, 1'b0);
  and and_51 (and_51_out, decoder_1_out2, 1'b0);
  and and_52 (and_52_out, decoder_1_out3, 1'b0);
  and and_53 (and_53_out, decoder_1_out4, 1'b1);
  and and_54 (and_54_out, decoder_1_out5, 1'b0);
  and and_55 (and_55_out, decoder_1_out6, 1'b0);
  and and_56 (and_56_out, decoder_1_out7, 1'b1);
  and and_57 (and_57_out, decoder_1_out0, 1'b0);
  and and_58 (and_58_out, decoder_1_out1, 1'b0);
  and and_59 (and_59_out, decoder_1_out2, 1'b0);
  and and_60 (and_60_out, decoder_1_out3, 1'b1);
  and and_61 (and_61_out, decoder_1_out4, 1'b1);
  and and_62 (and_62_out, decoder_1_out5, 1'b1);
  and and_63 (and_63_out, decoder_1_out6, 1'b1);
  and and_64 (and_64_out, decoder_1_out7, 1'b1);
  or or_6 (Q2, and_41_out, and_42_out, and_43_out, and_44_out, and_45_out, and_46_out, and_47_out, and_48_out);
  or or_7 (Q1, and_49_out, and_50_out, and_51_out, and_52_out, and_53_out, and_54_out, and_55_out, and_56_out);
  or or_8 (Q0, and_57_out, and_58_out, and_59_out, and_60_out, and_61_out, and_62_out, and_63_out, and_64_out);
endmodule

module Random_access_memory (
  input  D7,
  input  D6,
  input  D4,
  input  D3,
  input  D5,
  input  D2,
  input  D1,
  input  D0,
  input  RESET,
  input  ENABLE2,
  input  A1,
  input  A0,
  input  ENBALE1,
  output Q1,
  output Q0,
  output Q3,
  output Q2,
  output Q5,
  output Q4,
  output Q7,
  output Q6
);

  wire and_1_out, and_2_out, and_3_out, and_4_out, and_5_out, and_6_out, and_7_out, and_8_out, and_9_out,
       and_10_out, and_11_out, and_12_out, and_13_out, and_14_out, and_15_out, and_16_out, and_17_out,
       and_18_out, and_19_out, and_20_out, and_21_out, and_22_out, and_23_out, and_24_out, and_25_out,
       and_26_out, and_27_out, and_28_out, and_29_out, and_30_out, and_31_out, and_32_out, and_33_out,
       and_34_out, and_35_out, and_36_out, CLK_out, decoder_1_out0, decoder_1_out1, decoder_1_out2,
       decoder_1_out3, enable_d_flip_flop_1_q, enable_d_flip_flop_2_q, enable_d_flip_flop_3_q,
       enable_d_flip_flop_4_q, enable_d_flip_flop_5_q, enable_d_flip_flop_6_q, enable_d_flip_flop_7_q,
       enable_d_flip_flop_8_q, enable_d_flip_flop_9_q, enable_d_flip_flop_10_q, enable_d_flip_flop_11_q,
       enable_d_flip_flop_12_q, enable_d_flip_flop_13_q, enable_d_flip_flop_14_q, enable_d_flip_flop_15_q,
       enable_d_flip_flop_16_q, enable_d_flip_flop_17_q, enable_d_flip_flop_18_q, enable_d_flip_flop_19_q,
       enable_d_flip_flop_20_q, enable_d_flip_flop_21_q, enable_d_flip_flop_22_q, enable_d_flip_flop_23_q,
       enable_d_flip_flop_24_q, enable_d_flip_flop_25_q, enable_d_flip_flop_26_q, enable_d_flip_flop_27_q,
       enable_d_flip_flop_28_q, enable_d_flip_flop_29_q, enable_d_flip_flop_30_q, enable_d_flip_flop_31_q,
       enable_d_flip_flop_32_q;
  wire [1:0] register_8bit_1_q0;

  Clock CLK (.out(CLK_out));
  Register_8bit register_8bit_1 (
    .CLK(CLK_out), .RESET(RESET), .D1(A1), .D0(A0), .ENABLE(ENBALE1), .Q1(register_8bit_1_q0[1]),
    .Q0(register_8bit_1_q0[0]));  // open: D7, D6, D5, D4, D3, D2, Q7, Q6, Q5, Q4, Q3, Q2
  Decoder #(.select(2)) decoder_1 (
    .out0(decoder_1_out0), .out1(decoder_1_out1), .out2(decoder_1_out2), .out3(decoder_1_out3),
    .sel(register_8bit_1_q0), .en(1'b1));
  and and_1 (and_1_out, decoder_1_out0, ENABLE2);
  and and_2 (and_2_out, decoder_1_out1, ENABLE2);
  and and_3 (and_3_out, decoder_1_out2, ENABLE2);
  and and_4 (and_4_out, decoder_1_out3, ENABLE2);
  Enable_D_flip_flop enable_d_flip_flop_1 (
    .CLK(CLK_out), .D(D7), .ENABLE(and_1_out), .Q(enable_d_flip_flop_1_q));  // open: NOTQ
  Enable_D_flip_flop enable_d_flip_flop_2 (
    .CLK(CLK_out), .D(D7), .ENABLE(and_2_out), .Q(enable_d_flip_flop_2_q));  // open: NOTQ
  Enable_D_flip_flop enable_d_flip_flop_3 (
    .CLK(CLK_out), .D(D7), .ENABLE(and_3_out), .Q(enable_d_flip_flop_3_q));  // open: NOTQ
  Enable_D_flip_flop enable_d_flip_flop_4 (
    .CLK(CLK_out), .D(D7), .ENABLE(and_4_out), .Q(enable_d_flip_flop_4_q));  // open: NOTQ
  and and_5 (and_5_out, enable_d_flip_flop_1_q, decoder_1_out0);
  and and_6 (and_6_out, enable_d_flip_flop_2_q, decoder_1_out1);
  and and_7 (and_7_out, enable_d_flip_flop_3_q, decoder_1_out2);
  and and_8 (and_8_out, enable_d_flip_flop_4_q, decoder_1_out3);
  or or_1 (Q7, and_8_out, and_7_out, and_6_out, and_5_out);
  Enable_D_flip_flop enable_d_flip_flop_5 (
    .CLK(CLK_out), .D(D6), .ENABLE(and_1_out), .Q(enable_d_flip_flop_5_q));  // open: NOTQ
  Enable_D_flip_flop enable_d_flip_flop_6 (
    .CLK(CLK_out), .D(D6), .ENABLE(and_2_out), .Q(enable_d_flip_flop_6_q));  // open: NOTQ
  Enable_D_flip_flop enable_d_flip_flop_7 (
    .CLK(CLK_out), .D(D6), .ENABLE(and_3_out), .Q(enable_d_flip_flop_7_q));  // open: NOTQ
  Enable_D_flip_flop enable_d_flip_flop_8 (
    .CLK(CLK_out), .D(D6), .ENABLE(and_4_out), .Q(enable_d_flip_flop_8_q));  // open: NOTQ
  and and_9 (and_9_out, enable_d_flip_flop_5_q, decoder_1_out0);
  and and_10 (and_10_out, enable_d_flip_flop_6_q, decoder_1_out1);
  and and_11 (and_11_out, enable_d_flip_flop_7_q, decoder_1_out2);
  and and_12 (and_12_out, enable_d_flip_flop_8_q, decoder_1_out3);
  or or_2 (Q6, and_12_out, and_11_out, and_10_out, and_9_out);
  Enable_D_flip_flop enable_d_flip_flop_9 (
    .CLK(CLK_out), .D(D5), .ENABLE(and_1_out), .Q(enable_d_flip_flop_9_q));  // open: NOTQ
  Enable_D_flip_flop enable_d_flip_flop_10 (
    .CLK(CLK_out), .D(D5), .ENABLE(and_2_out), .Q(enable_d_flip_flop_10_q));  // open: NOTQ
  Enable_D_flip_flop enable_d_flip_flop_11 (
    .CLK(CLK_out), .D(D5), .ENABLE(and_3_out), .Q(enable_d_flip_flop_11_q));  // open: NOTQ
  Enable_D_flip_flop enable_d_flip_flop_12 (
    .CLK(CLK_out), .D(D5), .ENABLE(and_4_out), .Q(enable_d_flip_flop_12_q));  // open: NOTQ
  and and_13 (and_13_out, enable_d_flip_flop_9_q, decoder_1_out0);
  and and_14 (and_14_out, enable_d_flip_flop_10_q, decoder_1_out1);
  and and_15 (and_15_out, enable_d_flip_flop_11_q, decoder_1_out2);
  and and_16 (and_16_out, enable_d_flip_flop_12_q, decoder_1_out3);
  or or_3 (Q5, and_16_out, and_15_out, and_14_out, and_13_out);
  Enable_D_flip_flop enable_d_flip_flop_13 (
    .CLK(CLK_out), .D(D4), .ENABLE(and_1_out), .Q(enable_d_flip_flop_13_q));  // open: NOTQ
  Enable_D_flip_flop enable_d_flip_flop_14 (
    .CLK(CLK_out), .D(D4), .ENABLE(and_2_out), .Q(enable_d_flip_flop_14_q));  // open: NOTQ
  Enable_D_flip_flop enable_d_flip_flop_15 (
    .CLK(CLK_out), .D(D4), .ENABLE(and_3_out), .Q(enable_d_flip_flop_15_q));  // open: NOTQ
  Enable_D_flip_flop enable_d_flip_flop_16 (
    .CLK(CLK_out), .D(D4), .ENABLE(and_4_out), .Q(enable_d_flip_flop_16_q));  // open: NOTQ
  and and_17 (and_17_out, enable_d_flip_flop_13_q, decoder_1_out0);
  and and_18 (and_18_out, enable_d_flip_flop_14_q, decoder_1_out1);
  and and_19 (and_19_out, enable_d_flip_flop_15_q, decoder_1_out2);
  and and_20 (and_20_out, enable_d_flip_flop_16_q, decoder_1_out3);
  or or_4 (Q4, and_20_out, and_19_out, and_18_out, and_17_out);
  Enable_D_flip_flop enable_d_flip_flop_17 (
    .CLK(CLK_out), .D(D3), .ENABLE(and_1_out), .Q(enable_d_flip_flop_17_q));  // open: NOTQ
  Enable_D_flip_flop enable_d_flip_flop_18 (
    .CLK(CLK_out), .D(D3), .ENABLE(and_2_out), .Q(enable_d_flip_flop_18_q));  // open: NOTQ
  Enable_D_flip_flop enable_d_flip_flop_19 (
    .CLK(CLK_out), .D(D3), .ENABLE(and_3_out), .Q(enable_d_flip_flop_19_q));  // open: NOTQ
  Enable_D_flip_flop enable_d_flip_flop_20 (
    .CLK(CLK_out), .D(D3), .ENABLE(and_4_out), .Q(enable_d_flip_flop_20_q));  // open: NOTQ
  and and_21 (and_21_out, enable_d_flip_flop_17_q, decoder_1_out0);
  and and_22 (and_22_out, enable_d_flip_flop_18_q, decoder_1_out1);
  and and_23 (and_23_out, enable_d_flip_flop_19_q, decoder_1_out2);
  and and_24 (and_24_out, enable_d_flip_flop_20_q, decoder_1_out3);
  or or_5 (Q3, and_24_out, and_23_out, and_22_out, and_21_out);
  Enable_D_flip_flop enable_d_flip_flop_21 (
    .CLK(CLK_out), .D(D2), .ENABLE(and_1_out), .Q(enable_d_flip_flop_21_q));  // open: NOTQ
  Enable_D_flip_flop enable_d_flip_flop_22 (
    .CLK(CLK_out), .D(D2), .ENABLE(and_2_out), .Q(enable_d_flip_flop_22_q));  // open: NOTQ
  Enable_D_flip_flop enable_d_flip_flop_23 (
    .CLK(CLK_out), .D(D2), .ENABLE(and_3_out), .Q(enable_d_flip_flop_23_q));  // open: NOTQ
  Enable_D_flip_flop enable_d_flip_flop_24 (
    .CLK(CLK_out), .D(D2), .ENABLE(and_4_out), .Q(enable_d_flip_flop_24_q));  // open: NOTQ
  and and_25 (and_25_out, enable_d_flip_flop_21_q, decoder_1_out0);
  and and_26 (and_26_out, enable_d_flip_flop_22_q, decoder_1_out1);
  and and_27 (and_27_out, enable_d_flip_flop_23_q, decoder_1_out2);
  and and_28 (and_28_out, enable_d_flip_flop_24_q, decoder_1_out3);
  or or_6 (Q2, and_28_out, and_27_out, and_26_out, and_25_out);
  Enable_D_flip_flop enable_d_flip_flop_25 (
    .CLK(CLK_out), .D(D1), .ENABLE(and_1_out), .Q(enable_d_flip_flop_25_q));  // open: NOTQ
  Enable_D_flip_flop enable_d_flip_flop_26 (
    .CLK(CLK_out), .D(D1), .ENABLE(and_2_out), .Q(enable_d_flip_flop_26_q));  // open: NOTQ
  Enable_D_flip_flop enable_d_flip_flop_27 (
    .CLK(CLK_out), .D(D1), .ENABLE(and_3_out), .Q(enable_d_flip_flop_27_q));  // open: NOTQ
  Enable_D_flip_flop enable_d_flip_flop_28 (
    .CLK(CLK_out), .D(D1), .ENABLE(and_4_out), .Q(enable_d_flip_flop_28_q));  // open: NOTQ
  and and_29 (and_29_out, enable_d_flip_flop_25_q, decoder_1_out0);
  and and_30 (and_30_out, enable_d_flip_flop_26_q, decoder_1_out1);
  and and_31 (and_31_out, enable_d_flip_flop_27_q, decoder_1_out2);
  and and_32 (and_32_out, enable_d_flip_flop_28_q, decoder_1_out3);
  or or_7 (Q1, and_32_out, and_31_out, and_30_out, and_29_out);
  Enable_D_flip_flop enable_d_flip_flop_29 (
    .CLK(CLK_out), .D(D0), .ENABLE(and_1_out), .Q(enable_d_flip_flop_29_q));  // open: NOTQ
  Enable_D_flip_flop enable_d_flip_flop_30 (
    .CLK(CLK_out), .D(D0), .ENABLE(and_2_out), .Q(enable_d_flip_flop_30_q));  // open: NOTQ
  Enable_D_flip_flop enable_d_flip_flop_31 (
    .CLK(CLK_out), .D(D0), .ENABLE(and_3_out), .Q(enable_d_flip_flop_31_q));  // open: NOTQ
  Enable_D_flip_flop enable_d_flip_flop_32 (
    .CLK(CLK_out), .D(D0), .ENABLE(and_4_out), .Q(enable_d_flip_flop_32_q));  // open: NOTQ
  and and_33 (and_33_out, enable_d_flip_flop_29_q, decoder_1_out0);
  and and_34 (and_34_out, enable_d_flip_flop_30_q, decoder_1_out1);
  and and_35 (and_35_out, enable_d_flip_flop_31_q, decoder_1_out2);
  and and_36 (and_36_out, enable_d_flip_flop_32_q, decoder_1_out3);
  or or_8 (Q0, and_36_out, and_35_out, and_34_out, and_33_out);
endmodule
