// Logisim project sequential_logic_circuit.circ as structural Verilog: 2 circuits, main circuit SR_latch_norgate
module SR_latch_norgate (
  output out_1,
  output out_2
);

  wire and_1_out, and_2_out, dipswitch_1_sw1, dipswitch_1_sw2, dipswitch_1_sw3;

  DipSwitch dipswitch_1 (
    .sw1(dipswitch_1_sw1), .sw2(dipswitch_1_sw2), .sw3(dipswitch_1_sw3));  // open: sw4, sw5, sw6, sw7, sw8
  and and_1 (and_1_out, dipswitch_1_sw1, dipswitch_1_sw2);
  and and_2 (and_2_out, dipswitch_1_sw2, dipswitch_1_sw3);
  nor nor_1 (out_1, and_1_out, out_2);
  nor nor_2 (out_2, out_1, and_2_out);
endmodule

module SR_latch_NANDgate (
  output out_1,
  output out_2
);

  wire and_1_out, and_2_out, dipswitch_1_sw1, dipswitch_1_sw2, dipswitch_1_sw3;

  DipSwitch dipswitch_1 (
    .sw1(dipswitch_1_sw1), .sw2(dipswitch_1_sw2), .sw3(dipswitch_1_sw3));  // open: sw4, sw5, sw6, sw7, sw8
  and and_1 (and_1_out, dipswitch_1_sw1, dipswitch_1_sw2);
  and and_2 (and_2_out, dipswitch_1_sw2, dipswitch_1_sw3);
  nand nand_1 (out_1, out_2, and_1_out);
  nand nand_2 (out_2, out_1, and_2_out);
endmodule
